// Logisim project LEDGame.circ as structural Verilog: 10 circuits, main circuit main
module main (
);

  wire button_1_out, button_2_out, button_3_out, controller_1_out_4, controller_1_out_5, controller_1_out_6,
       controller_1_out_7, controller_1_out_8, controller_1_out_9, controller_1_out_10, controller_1_out_11,
       controller_1_out_12, controller_1_out_13, controller_1_out_14, controller_1_out_15,
       controller_1_out_16, controller_1_out_17, controller_1_out_18, controller_1_out_19,
       controller_1_out_20, controller_1_out_21, controller_1_out_22, controller_1_out_23,
       controller_1_out_24, controller_1_out_25, controller_1_out_26;

  Controller controller_1 (
    .in_1(button_1_out), .in_2(button_3_out), .out_4(controller_1_out_4), .out_5(controller_1_out_5),
    .out_6(controller_1_out_6), .out_7(controller_1_out_7), .out_8(controller_1_out_8),
    .out_9(controller_1_out_9), .out_10(controller_1_out_10), .Reset_In(button_2_out),
    .out_11(controller_1_out_11), .out_12(controller_1_out_12), .out_13(controller_1_out_13),
    .out_14(controller_1_out_14), .out_19(controller_1_out_19), .out_20(controller_1_out_20),
    .out_21(controller_1_out_21), .out_22(controller_1_out_22), .out_15(controller_1_out_15),
    .out_16(controller_1_out_16), .out_17(controller_1_out_17), .out_18(controller_1_out_18),
    .out_23(controller_1_out_23), .out_24(controller_1_out_24), .out_25(controller_1_out_25),
    .out_26(controller_1_out_26));
  LED led_1 (.in(controller_1_out_4));
  LED led_2 (.in(controller_1_out_5));
  _7_Segment_Display u_7_segment_display_1 (
    .g(controller_1_out_11), .f(controller_1_out_12), .a(controller_1_out_13), .b(controller_1_out_14),
    .e(controller_1_out_19), .d(controller_1_out_20), .c(controller_1_out_21), .dp(controller_1_out_22));
  Button button_1 (.out(button_1_out));
  LED led_3 (.in(controller_1_out_7));
  LED led_4 (.in(controller_1_out_6));
  Button button_2 (.out(button_2_out));
  LED led_5 (.in(controller_1_out_8));
  LED led_6 (.in(controller_1_out_9));
  _7_Segment_Display u_7_segment_display_2 (
    .g(controller_1_out_15), .f(controller_1_out_16), .a(controller_1_out_17), .b(controller_1_out_18),
    .e(controller_1_out_23), .d(controller_1_out_24), .c(controller_1_out_25), .dp(controller_1_out_26));
  LED led_7 (.in(controller_1_out_10));
  Button button_3 (.out(button_3_out));

  // Notes on the sheet:
  //   Player 1
  //   LED GAME
  //   Reset
  //   Made by Rahmet Ali Olmez
  //   2020
  //   Player 2
  //   Recommended Minimum Clock Rate: 64Hz
  //   Make sure the clock is turned on
  //   and the simulation is enabled.
endmodule

module N0 (
  input  b1,
  input  b2,
  input  in_3,
  input  in_4,
  input  in_5,
  output Output
);

  wire and_1_out, and_2_out, and_3_out, and_4_out, and_5_out, not_1_out;

  not not_1 (not_1_out, b1);
  and and_1 (and_1_out, not_1_out, in_5);
  and and_2 (and_2_out, in_3, in_5);
  and and_3 (and_3_out, in_5, in_4);
  and and_4 (and_4_out, b2, in_5);
  and and_5 (and_5_out, not_1_out, b2, in_4, in_3);
  or or_1 (Output, and_1_out, and_2_out, and_3_out, and_4_out, and_5_out);

  // Notes on the sheet:
  //   s2
  //   s1
  //   s0
endmodule

module N1 (
  input  b1,
  input  b2,
  input  in_3,
  input  in_4,
  input  in_5,
  output Output
);

  wire and_1_out, and_2_out, and_3_out, and_4_out, and_5_out, and_6_out, not_1_out, not_2_out, not_3_out,
       not_4_out, not_5_out, not_6_out;

  not not_1 (not_1_out, b2);
  not not_2 (not_2_out, b1);
  not not_3 (not_3_out, b1);
  and and_1 (and_1_out, in_4, in_5);
  not not_4 (not_4_out, b2);
  not not_5 (not_5_out, in_3);
  and and_2 (and_2_out, not_2_out, not_1_out, in_4);
  not not_6 (not_6_out, in_4);
  and and_3 (and_3_out, b2, in_4, not_5_out);
  and and_4 (and_4_out, b1, in_4, in_3);
  and and_5 (and_5_out, not_3_out, b2, not_6_out, in_3);
  and and_6 (and_6_out, b1, not_4_out, in_5, not_5_out);
  or or_1 (Output, and_1_out, and_2_out, and_3_out, and_4_out, and_5_out, and_6_out);

  // Notes on the sheet:
  //   s2
  //   s1
  //   s0
endmodule

module N2 (
  input  b1,
  input  b2,
  input  in_3,
  input  in_4,
  input  in_5,
  output Output
);

  wire and_1_out, and_2_out, and_3_out, and_4_out, and_5_out, and_7_out, not_1_out, not_2_out, not_3_out,
       not_4_out, not_5_out, not_6_out, not_7_out, not_8_out, not_9_out;

  not not_1 (not_1_out, b2);
  not not_2 (not_2_out, b1);
  and and_1 (and_1_out, b1, b2, in_3);
  not not_3 (not_3_out, in_4);
  not not_4 (not_4_out, in_3);
  and and_2 (and_2_out, b1, not_1_out, not_4_out, not_3_out, in_5);
  not not_5 (not_5_out, in_5);
  not not_6 (not_6_out, b2);
  and and_3 (and_3_out, b1, not_6_out, not_5_out, in_4, not_4_out);
  not not_7 (not_7_out, b1);
  and and_4 (and_4_out, not_7_out, b2, in_5, not_3_out, not_4_out);
  not not_8 (not_8_out, b2);
  not not_9 (not_9_out, in_5);
  and and_5 (and_5_out, not_2_out, b2, not_9_out, in_4, not_4_out);
  // AND_Gate and_6 has open pins: in0=not_2_out, in1=not_8_out, in2=not_9_out, in3=not_3_out, out=open
  and and_7 (and_7_out, not_2_out, not_8_out, in_3);
  or or_1 (Output, and_1_out, and_2_out, and_3_out, and_4_out, and_5_out, and_7_out);

  // Notes on the sheet:
  //   s2
  //   s1
  //   s0
endmodule

module CombinationalLogic (
  input  b1,
  input  b2,
  input  Reset_In,
  input  in_4,
  input  in_5,
  input  in_6,
  output out_7,
  output out_8,
  output out_9,
  output out_10,
  output out_11,
  output out_12,
  output out_13,
  output out_14,
  output n0,
  output n1
);

  wire buttonmanager_1_out_2, buttonmanager_2_out_2, n0_1_output, n1_1_output, n2_1_output;

  ButtonManager buttonmanager_1 (.in_1(b1), .out_2(buttonmanager_1_out_2));
  ButtonManager buttonmanager_2 (.in_1(b2), .out_2(buttonmanager_2_out_2));
  N0 n0_1 (
    .b1(buttonmanager_1_out_2), .b2(buttonmanager_2_out_2), .in_3(in_4), .in_4(in_5), .in_5(in_6),
    .Output(n0_1_output));
  N1 n1_1 (
    .b1(buttonmanager_1_out_2), .b2(buttonmanager_2_out_2), .Output(n1_1_output), .in_3(in_4), .in_4(in_5),
    .in_5(in_6));
  N2 n2_1 (
    .b1(buttonmanager_1_out_2), .b2(buttonmanager_2_out_2), .Output(n2_1_output), .in_3(in_4), .in_4(in_5),
    .in_5(in_6));
  Reset reset_1 (
    ._0(n0_1_output), ._1(n1_1_output), ._2(n2_1_output), .out_5(n0), .out_6(out_14), .out_7(n1),
    .Reset_In(Reset_In));
  Decoder #(.select(3)) decoder_1 (
    .out0(out_7), .out1(out_8), .out2(out_9), .out3(out_10), .out4(out_11), .out5(out_12), .out6(out_13),
    .sel({n0, out_14, n1}));  // open: out7, en

  // Notes on the sheet:
  //   s2
  //   s1
  //   s0
  //   n2
endmodule

module Controller (
  input  in_1,
  input  in_2,
  input  Reset_In,
  output out_4,
  output out_5,
  output out_6,
  output out_7,
  output out_8,
  output out_9,
  output out_10,
  output out_11,
  output out_12,
  output out_13,
  output out_14,
  output out_15,
  output out_16,
  output out_17,
  output out_18,
  output out_19,
  output out_20,
  output out_21,
  output out_22,
  output out_23,
  output out_24,
  output out_25,
  output out_26
);

  wire clock_1_out;
  wire [2:0] combinationallogic_1_n1, register_1_q;

  CombinationalLogic combinationallogic_1 (
    .b1(in_1), .b2(in_2), .in_4(register_1_q[0]), .in_5(register_1_q[1]), .in_6(register_1_q[2]),
    .n0(combinationallogic_1_n1[2]), .out_14(combinationallogic_1_n1[1]), .n1(combinationallogic_1_n1[0]),
    .out_7(out_4), .out_8(out_5), .out_9(out_6), .out_10(out_7), .out_11(out_8), .out_12(out_9),
    .out_13(out_10), .Reset_In(Reset_In));
  Register #(.width(3)) register_1 (.D(combinationallogic_1_n1), .Q(register_1_q), .clk(clock_1_out));  // open: en, clr
  Clock clock_1 (.out(clock_1_out));
  ScoreCounter scorecounter_1 (
    .in_1(out_4), .out_2(out_11), .out_3(out_12), .out_4(out_13), .out_5(out_14), .out_6(out_19),
    .out_7(out_20), .out_8(out_21), .out_9(out_22));
  ScoreCounter scorecounter_2 (
    .in_1(out_10), .out_2(out_15), .out_3(out_16), .out_4(out_17), .out_5(out_18), .out_6(out_23),
    .out_7(out_24), .out_8(out_25), .out_9(out_26));
endmodule

module ButtonManager (
  input  in_1,
  output out_2
);

  wire and_1_out, and_2_out, clock_1_out, not_1_out, not_2_out;
  wire [0:0] or_1_out;
  wire [1:0] register_1_q;

  and and_1 (and_1_out, in_1, register_1_q[1], not_2_out);
  not not_1 (not_1_out, register_1_q[1]);
  not not_2 (not_2_out, register_1_q[0]);
  Register #(.width(2)) register_1 (.D({out_2, or_1_out[0]}), .Q(register_1_q), .clk(clock_1_out));  // open: en, clr
  Clock clock_1 (.out(clock_1_out));
  and and_2 (and_2_out, in_1, register_1_q[0], not_1_out);
  or or_1 (or_1_out[0], and_1_out, and_2_out);
  and and_3 (out_2, in_1, not_2_out, not_1_out);
endmodule

module Reset (
  input  _0,
  input  _1,
  input  _2,
  input  Reset_In,
  output out_5,
  output out_6,
  output out_7
);

  wire not_1_out;

  not not_1 (not_1_out, Reset_In);
  and and_1 (out_5, _0, not_1_out);
  or or_1 (out_6, _1, Reset_In);
  or or_2 (out_7, _2, Reset_In);
endmodule

module ScoreCounter (
  input  in_1,
  output out_2,
  output out_3,
  output out_4,
  output out_5,
  output out_6,
  output out_7,
  output out_8,
  output out_9
);

  wire buttonmanager_1_out_2, clock_1_out, decoder_1_out0, decoder_1_out1, decoder_1_out2, decoder_1_out3,
       decoder_1_out4, decoder_1_out5, decoder_1_out6, decoder_1_out7;
  wire [2:0] counter_1_q;

  ButtonManager buttonmanager_1 (.in_1(in_1), .out_2(buttonmanager_1_out_2));
  Clock clock_1 (.out(clock_1_out));
  Counter #(.width(3), .max('h7)) counter_1 (
    .count(buttonmanager_1_out_2), .Q(counter_1_q), .clk(clock_1_out));  // open: load, D, carry, clr
  Decoder #(.select(3)) decoder_1 (
    .out0(decoder_1_out0), .out1(decoder_1_out1), .out2(decoder_1_out2), .out3(decoder_1_out3),
    .out4(decoder_1_out4), .out5(decoder_1_out5), .out6(decoder_1_out6), .out7(decoder_1_out7),
    .sel(counter_1_q));  // open: en
  NumberConverter numberconverter_1 (
    ._0(decoder_1_out0), ._1(decoder_1_out1), ._2(decoder_1_out2), ._3(decoder_1_out3), ._4(decoder_1_out4),
    ._5(decoder_1_out5), ._6(decoder_1_out6), ._7(decoder_1_out7), .out_9(out_2), .out_10(out_3),
    .out_11(out_4), .out_12(out_5), .out_13(out_6), .out_14(out_7), .out_15(out_8), .out_16(out_9));
endmodule

module NumberConverter (
  input  _0,
  input  _1,
  input  _2,
  input  _3,
  input  _4,
  input  _5,
  input  _6,
  input  _7,
  output out_9,
  output out_10,
  output out_11,
  output out_12,
  output out_13,
  output out_14,
  output out_15,
  output out_16
);

  or or_1 (out_9, _2, _3, _4, _5, _6);
  or or_2 (out_13, _0, _2, _6);
  or or_3 (out_10, _0, _4, _5, _6);
  or or_4 (out_14, _0, _2, _3, _5, _6);
  or or_5 (out_11, _0, _2, _3, _5, _6, _7);
  or or_6 (out_15, _0, _1, _3, _4, _5, _6, _7);
  or or_7 (out_12, _0, _1, _2, _3, _4, _7);
  buf or_8 (out_16, _7);  // OR_Gate
endmodule
